// Digital circuit full_adder.dig as structural Verilog
module full_adder (
  input  C_In,
  input  A,
  input  B,
  output Sum_Final,
  output C_Final
);

  wire and_1_out, and_2_out, xor_1_out;

  xor xor_1 (xor_1_out, A, B);
  and and_1 (and_1_out, B, A);
  xor xor_2 (Sum_Final, xor_1_out, C_In);
  and and_2 (and_2_out, C_In, xor_1_out);
  or or_1 (C_Final, and_2_out, and_1_out);
endmodule
